# Fritzing sketch body (saved by Fritzing 0.9.3b)
breadboards: 1

parts:
  R1 = Resistor [tolerance=±5% resistance=560 package=THT]
  R2 = Resistor [tolerance=±5% resistance=560 package=THT]
  R3 = Resistor [tolerance=±5% resistance=560 package=THT]
  R4 = Resistor [tolerance=±5% resistance=560 package=THT]
  U2 = 74HC595 [package="DIP16 [THT]"]
  U3 = 74HC595 [package="DIP16 [THT]"]
  Part1 = Arduino Uno (Rev3)
  ON/OFF_BUTTON = SWITCH-MOMENTARY-2 [package=tactile-pth-12mm]
  PATTERN_BUTTON = SWITCH-MOMENTARY-2 [package=tactile-pth-12mm]

nets:
  N1: R1.Pin_0, Part1.D11_PWM/MOSI
  N2: R2.Pin_0, Part1.D10_PWM/SS
  N3: R3.Pin_0, Part1.D9_PWM
  N4: R4.Pin_0, Part1.D6_PWM
  GND: U2.GND, U2.OE, U3.GND, U3.OE, Part1.GND, ON/OFF_BUTTON.2, PATTERN_BUTTON.2
  N5: U2.Q7', U3.DS
  VCC: U2.MR, U2.VCC, U3.MR, U3.VCC, Part1.5V
  N6: U2.SH_CP, U3.SH_CP, Part1.D3_PWM
  N7: U2.ST_CP, U3.ST_CP, Part1.D4
  N8: U2.DS, Part1.D2
  N9: Part1.D12/MISO, ON/OFF_BUTTON.1
  N10: Part1.D13/SCK, PATTERN_BUTTON.1

notes:
  ANODE1
  ANODE2
  ANODE3
  ANODE0
  CATHODE9
  CATHODE10
  CATHODE12
  CATHODE11
  CATHODE14
  CATHODE13
  CATHODE8
  CATHODE15
  CATHODE4
  CATHODE5
  CATHODE1
  CATHODE6
  CATHODE0
  CATHODE3
  CATHODE7
  CATHODE2
