# Fritzing sketch body_breadboard (saved by Fritzing 0.9.3b)
breadboards: 1

parts:
  Part1 = Arduino Uno (Rev3)
  U1 = 74HC595 [package="DIP16 [THT]"]
  U2 = 74HC595 [package="DIP16 [THT]"]
  R1 = Resistor [tolerance=±5% resistance=560 package="0603 [SMD]"]
  R2 = Resistor [tolerance=±5% resistance=560 package="0603 [SMD]"]
  R3 = Resistor [tolerance=±5% resistance=560 package="0603 [SMD]"]
  R4 = Resistor [tolerance=±5% resistance=560 package="0603 [SMD]"]
  S1 = Round Pushbutton
  S2 = Round Pushbutton

nets:
  N1: Part1.D9_PWM, R2.Pin_1
  N2: Part1.D10_PWM/SS, R3.Pin_1
  N3: Part1.D11_PWM/MOSI, R4.Pin_1
  N4: Part1.D12/MISO, S2.leg0
  N5: Part1.D13/SCK, S1.leg0
  N6: Part1.D2, U1.DS
  N7: Part1.D3_PWM, U1.SH_CP, U2.SH_CP
  N8: Part1.D4, U1.ST_CP, U2.ST_CP
  N9: Part1.D6_PWM, R1.Pin_1
  VCC: Part1.5V, U1.MR, U1.VCC, U2.MR, U2.VCC
  GND: Part1.GND, U1.GND, U1.OE, U2.GND, U2.OE, S1.leg1, S2.leg1
  N10: U1.Q7', U2.DS

notes:
  CATHODE8
  CATHODE13
  CATHODE14
  CATHODE11
  CATHODE12
  CATHODE10
  CATHODE9
  CATHODES
  ANODES
  CLOCK
