# Fritzing sketch leds (saved by Fritzing 0.9.3b)
breadboards: 1

parts:
  LED17 = LEDs [package=led10mm]
  LED18 = LEDs [package=led10mm]
  LED19 = LEDs [package=led10mm]
  LED20 = LEDs [package=led10mm]
  LED21 = LEDs [package=led10mm]
  LED22 = LEDs [package=led10mm]
  LED23 = LEDs [package=led10mm]
  LED24 = LEDs [package=led10mm]
  LED25 = LEDs [package=led10mm]
  LED26 = LEDs [package=led10mm]
  LED27 = LEDs [package=led10mm]
  LED28 = LEDs [package=led10mm]
  LED29 = LEDs [package=led10mm]
  LED30 = LEDs [package=led10mm]
  LED31 = LEDs [package=led10mm]
  LED32 = LEDs [package=led10mm]
  LED65 = LEDs [package=led10mm]
  LED66 = LEDs [package=led10mm]
  LED67 = LEDs [package=led10mm]
  LED68 = LEDs [package=led10mm]
  LED69 = LEDs [package=led10mm]
  LED70 = LEDs [package=led10mm]
  LED71 = LEDs [package=led10mm]
  LED72 = LEDs [package=led10mm]
  LED73 = LEDs [package=led10mm]
  LED74 = LEDs [package=led10mm]
  LED75 = LEDs [package=led10mm]
  LED76 = LEDs [package=led10mm]
  LED77 = LEDs [package=led10mm]
  LED78 = LEDs [package=led10mm]
  LED79 = LEDs [package=led10mm]
  LED80 = LEDs [package=led10mm]
  LED81 = LEDs [package=led10mm]
  LED82 = LEDs [package=led10mm]
  LED83 = LEDs [package=led10mm]
  LED84 = LEDs [package=led10mm]
  LED85 = LEDs [package=led10mm]
  LED86 = LEDs [package=led10mm]
  LED87 = LEDs [package=led10mm]
  LED88 = LEDs [package=led10mm]
  LED89 = LEDs [package=led10mm]
  LED90 = LEDs [package=led10mm]
  LED91 = LEDs [package=led10mm]
  LED92 = LEDs [package=led10mm]
  LED93 = LEDs [package=led10mm]
  LED94 = LEDs [package=led10mm]
  LED95 = LEDs [package=led10mm]
  LED96 = LEDs [package=led10mm]
  LED97 = LEDs [package=led10mm]
  LED98 = LEDs [package=led10mm]
  LED99 = LEDs [package=led10mm]
  LED100 = LEDs [package=led10mm]
  LED101 = LEDs [package=led10mm]
  LED102 = LEDs [package=led10mm]
  LED103 = LEDs [package=led10mm]
  LED104 = LEDs [package=led10mm]
  LED105 = LEDs [package=led10mm]
  LED106 = LEDs [package=led10mm]
  LED107 = LEDs [package=led10mm]
  LED108 = LEDs [package=led10mm]
  LED109 = LEDs [package=led10mm]
  LED110 = LEDs [package=led10mm]
  LED111 = LEDs [package=led10mm]
  LED112 = LEDs [package=led10mm]

nets:
  N1: LED17.A, LED18.A, LED19.A, LED20.A, LED21.A, LED22.A, LED23.A, LED24.A, LED25.A, LED26.A, LED27.A, LED28.A, LED29.A, LED30.A, LED31.A, LED32.A
  N2: LED65.A, LED66.A, LED67.A, LED68.A, LED69.A, LED70.A, LED71.A, LED72.A, LED73.A, LED74.A, LED75.A, LED76.A, LED77.A, LED78.A, LED79.A, LED80.A
  N3: LED81.A, LED83.A, LED85.A, LED87.A, LED89.A, LED91.A, LED93.A, LED95.A, LED97.A, LED99.A, LED101.A, LED103.A, LED105.A, LED107.A, LED109.A, LED111.A
  N4: LED82.A, LED84.A, LED86.A, LED88.A, LED90.A, LED92.A, LED94.A, LED96.A, LED98.A, LED100.A, LED102.A, LED104.A, LED106.A, LED108.A, LED110.A, LED112.A

notes:
  LAYER
  L1
  ANODE0
  CATHODE0    CATHODE1    CATHODE2      CATHODE3
  CATHODE4    CATHODE5    CATHODE6      CATHODE7
  CATHODE8    CATHODE9    CATHODE10      CATHODE11
  CATHODE12    CATHODE13    CATHODE14      CATHODE15
  ANODE3
  ANODE1
  ANODE4
