# Fritzing sketch body (saved by Fritzing 0.9.3b)
breadboards: 1

parts:
  R1 = Resistor [tolerance=±5% resistance=560 package=THT]
  R2 = Resistor [tolerance=±5% resistance=560 package=THT]
  R3 = Resistor [tolerance=±5% resistance=560 package=THT]
  R4 = Resistor [tolerance=±5% resistance=560 package=THT]
  U1 = 74HC595 [package="DIP16 [THT]"]
  U2 = 74HC595 [package="DIP16 [THT]"]
  U3 = 74HC595 [package="DIP16 [THT]"]
  Part1 = Arduino Uno (Rev3)  # not connected

nets:
  N1: R1.Pin_0, U1.Q0
  N2: R2.Pin_0, U1.Q1
  N3: R3.Pin_0, U1.Q2
  N4: R4.Pin_0, U1.Q3
  GND: U1.GND, U2.GND, U3.GND
  N5: U1.SH_CP, U2.SH_CP, U3.SH_CP
  N6: U1.ST_CP, U2.ST_CP, U3.ST_CP

notes:
  LAYER3
  LAYER2
  LAYER1
  LAYER4
  CATHODE9
  CATHODE10
  CATHODE12
  CATHODE11
  CATHODE14
  CATHODE13
  CATHODE8
  CATHODE15
  CATHODE4
  CATHODE5
  CATHODE1
  CATHODE6
  CATHODE0
  CATHODE3
  CATHODE7
  CATHODE2
