# Fritzing sketch leds (saved by Fritzing 0.9.3b)
breadboards: 1

parts:
  LED1 = LEDs [package=led10mm]
  LED2 = LEDs [package=led10mm]
  LED3 = LEDs [package=led10mm]
  LED4 = LEDs [package=led10mm]
  LED5 = LEDs [package=led10mm]
  LED6 = LEDs [package=led10mm]
  LED7 = LEDs [package=led10mm]
  LED8 = LEDs [package=led10mm]
  LED9 = LEDs [package=led10mm]
  LED10 = LEDs [package=led10mm]
  LED11 = LEDs [package=led10mm]
  LED12 = LEDs [package=led10mm]
  LED13 = LEDs [package=led10mm]
  LED14 = LEDs [package=led10mm]
  LED15 = LEDs [package=led10mm]
  LED16 = LEDs [package=led10mm]
  LED17 = LEDs [package=led10mm]
  LED18 = LEDs [package=led10mm]
  LED19 = LEDs [package=led10mm]
  LED20 = LEDs [package=led10mm]
  LED21 = LEDs [package=led10mm]
  LED22 = LEDs [package=led10mm]
  LED23 = LEDs [package=led10mm]
  LED24 = LEDs [package=led10mm]
  LED25 = LEDs [package=led10mm]
  LED26 = LEDs [package=led10mm]
  LED27 = LEDs [package=led10mm]
  LED28 = LEDs [package=led10mm]
  LED29 = LEDs [package=led10mm]
  LED30 = LEDs [package=led10mm]
  LED31 = LEDs [package=led10mm]
  LED32 = LEDs [package=led10mm]
  LED33 = LEDs [package=led10mm]
  LED34 = LEDs [package=led10mm]
  LED35 = LEDs [package=led10mm]
  LED36 = LEDs [package=led10mm]
  LED37 = LEDs [package=led10mm]
  LED38 = LEDs [package=led10mm]
  LED39 = LEDs [package=led10mm]
  LED40 = LEDs [package=led10mm]
  LED41 = LEDs [package=led10mm]
  LED42 = LEDs [package=led10mm]
  LED43 = LEDs [package=led10mm]
  LED44 = LEDs [package=led10mm]
  LED45 = LEDs [package=led10mm]
  LED46 = LEDs [package=led10mm]
  LED47 = LEDs [package=led10mm]
  LED48 = LEDs [package=led10mm]
  LED49 = LEDs [package=led10mm]
  LED50 = LEDs [package=led10mm]
  LED51 = LEDs [package=led10mm]
  LED52 = LEDs [package=led10mm]
  LED53 = LEDs [package=led10mm]
  LED54 = LEDs [package=led10mm]
  LED55 = LEDs [package=led10mm]
  LED56 = LEDs [package=led10mm]
  LED57 = LEDs [package=led10mm]
  LED58 = LEDs [package=led10mm]
  LED59 = LEDs [package=led10mm]
  LED60 = LEDs [package=led10mm]
  LED61 = LEDs [package=led10mm]
  LED62 = LEDs [package=led10mm]
  LED63 = LEDs [package=led10mm]
  LED64 = LEDs [package=led10mm]

nets:
  N1: LED1.A, LED2.A, LED3.A, LED4.A, LED5.A, LED6.A, LED7.A, LED8.A, LED9.A, LED10.A, LED11.A, LED12.A, LED13.A, LED14.A, LED15.A, LED16.A
  N2: LED17.A, LED18.A, LED19.A, LED20.A, LED21.A, LED22.A, LED23.A, LED24.A, LED25.A, LED26.A, LED27.A, LED28.A, LED29.A, LED30.A, LED31.A, LED32.A
  N3: LED33.A, LED34.A, LED35.A, LED36.A, LED37.A, LED38.A, LED39.A, LED40.A, LED41.A, LED42.A, LED43.A, LED44.A, LED45.A, LED46.A, LED47.A, LED48.A
  N4: LED49.A, LED50.A, LED51.A, LED52.A, LED53.A, LED54.A, LED55.A, LED56.A, LED57.A, LED58.A, LED59.A, LED60.A, LED61.A, LED62.A, LED63.A, LED64.A

notes:
  L1
  L2
  L3
  L4
  LAYER1
  L7
  L8
  L6
  L12
  L10
  L9
  L11
  L16
  L14
  L13
  L15
  LAYER
  LAYER2
  LAYER3
  LAYER4
